# Fritzing sketch Fridgeye (saved by Fritzing 0.9.3b)
breadboards: 1

parts:
  Part1 = Photon
  R2 = Resistor [tolerance=±5% resistance=330 package=THT]
  Photocell = Photocell (LDR) [package=THT]
  T1 = TMP36 Temperature Sensor [package="TO92 [THT]"]
  Piezo1 = Piezo Speaker - PC Mount [part_number=COM-07950]

nets:
  N1: Part1.A0, R2.Pin_0, Photocell.pin_0
  N2: Part1.A4, T1.Vout
  GND: Part1.GND, R2.Pin_1, T1.GND, Piezo1.GND
  N3: Part1.D3, Piezo1.VCC
  N4: Part1.3V3, Photocell.pin_1, T1.+Vs

notes:
  +
  -

custom parts:
  Piezo Speaker - PC Mount: This is a small 12mm round speaker that operates around the audible 2kHz range. You can use these speakers to create simple music or user interfaces. Each speaker is PTH solderable and requires an operating voltage of 3.5-5V with a mean current of 35mA max. These speakers also have a typical sound output of 95 dBA and a coil resistance of 42 ±6.3 ohms.
